# Fritzing sketch droidrone-servo2 (saved by Fritzing 0.9.3b)
perfboards: 2

parts:
  Arduino_Pro_Mini = Arduino Pro Mini v13
  RC-Rudder = Basic Servo
  Motor_Power_(ESC) = Basic Servo
  Camera-Tilt = Basic Servo
  Camera-Pan = Basic Servo
  US1881 = IC, SIP package, 3 pins [chip_label=IC]
  J4 = Dagu DGServo 9g header (male) [package=THT]
  S4 = Dagu DGServo 9g header connector (female) [package=THT]
  J3 = Dagu DGServo 9g header (male) [package=THT]
  J2 = Dagu DGServo 9g header (male) [package=THT]
  J1 = Dagu DGServo 9g header (male) [package=THT]
  S3 = Dagu DGServo 9g header connector (female) [package=THT]
  S2 = Dagu DGServo 9g header connector (female) [package=THT]
  S1 = Dagu DGServo 9g header connector (female) [package=THT]
  R1 = Resistor [tolerance=±5% resistance=10k package=THT]
  BT_SPP = Bluetooth HC-05 Macho
  BT_SPP_2 = Bluetooth HC-05 Macho  # not connected
  R3 = Resistor [tolerance=±1% resistance=1.5k package=THT]
  R2 = Resistor [tolerance=±1% resistance=1.5k package=THT]
  RC_BATT = female pin header, 2 pins [form="♀ (female)"]

nets:
  N1: Arduino_Pro_Mini.D0/TX, BT_SPP.TXD
  N2: Arduino_Pro_Mini.D1/RX, BT_SPP.RXD
  VCC: Arduino_Pro_Mini.VCC, US1881.pin1, J4.pulse, J3.pulse, J2.pulse, J1.pulse, R1.Pin_0, BT_SPP.VCC
  GND: Arduino_Pro_Mini.GND, US1881.pin2, J4.gnd, J3.gnd, J2.gnd, J1.gnd, BT_SPP.GND, R3.Pin_1, RC_BATT.pin1
  N3: Arduino_Pro_Mini.A0, R3.Pin_0, R2.Pin_1
  N4: Arduino_Pro_Mini.D10_PWM/SS, J1.Vcc
  N5: Arduino_Pro_Mini.D9_PWM, J2.Vcc
  N6: Arduino_Pro_Mini.D6_PWM, J3.Vcc
  N7: Arduino_Pro_Mini.D5_PWM, J4.Vcc
  N8: Arduino_Pro_Mini.D2, US1881.pin3, R1.Pin_1
  GND_2: RC-Rudder.gnd, S2.gnd
  VCC_2: RC-Rudder.vcc, S2.Vcc
  N9: RC-Rudder.pulse, S2.pulse
  GND_3: Motor_Power_(ESC).gnd, S1.gnd
  VCC_3: Motor_Power_(ESC).vcc, S1.Vcc
  N10: Motor_Power_(ESC).pulse, S1.pulse
  GND_4: Camera-Tilt.gnd, S3.gnd
  VCC_4: Camera-Tilt.vcc, S3.Vcc
  N11: Camera-Tilt.pulse, S3.pulse
  GND_5: Camera-Pan.gnd, S4.gnd
  VCC_5: Camera-Pan.vcc, S4.Vcc
  N12: Camera-Pan.pulse, S4.pulse
  N13: R2.Pin_0, RC_BATT.pin2

// code stored in the sketch: Untitled.ino




// ????????????????


/*

  http://tetsuakibaba.jp/index.php?page=workshop/ServoBasis/main

  ?????????????????

  r: ????????

  800-2200: 0??90???



  a: attach(9)

  d: detach()



  http://marupeke296.com/EL_Ard_No9_ServoMotor.html

  http://www.vstone.co.jp/vs_wiki/main/wiki.cgi?page=Arduino%A4%C7%BB%CF%A4%E1%A4%EB%A5%ED%A5%DC%A5%C3%A5%C8%C0%A9%B8%E6

  http://wacho.main.jp/Elec/Servo_Driver/Servo_Driver.html

  http://detail.chiebukuro.yahoo.co.jp/qa/question_detail/q14109772659

  http://otonaradicon.com/arrc/



  ????????????????????????????????

  http://akizukidenshi.com/catalog/g/gM-06682/

  ?????????????????????????????????????????????????????

  ??????? ??? ???? ???

  http://i.stack.imgur.com/oOtkU.png

  PWM??????????????Pin

*/



#include <Servo.h>



Servo sv9;

Servo sv10;

Servo sv5;

Servo sv6;

int analog9 = 0;

int analog10 = 0;

int i = 7;

int inPin = 2;   // ??????2??????

int hallVal = 0;     // ?????????????

int lasthallVal = 0;     // ???????????????

int hallCount = 0; //?????????

unsigned long lastTime;

boolean servoAttached = false;



void moveShaft(Servo sv, int pulse, long int delay_ms)

{

  int pulse_now = sv.readMicroseconds();



  if ( pulse > pulse_now ) {

    for ( int i = pulse_now; i <= pulse; i++ ) {

      sv.writeMicroseconds(i);

      delay(delay_ms);

    }

  }

  else if ( pulse < pulse_now ) {

    for ( int i = pulse_now; i >= pulse; i-- ) {

      sv.writeMicroseconds(i);

      delay(delay_ms);

    }

  }

  else {

    // do nothing

  }

}



void setup()

{

  Serial.begin(9600);

  pinMode(13, OUTPUT); //LED??

  //???????????????? http://akizukidenshi.com/catalog/g/gI-05274/

  //??????????

  //???????????????????????? http://play-arduino.seesaa.net/article/427884258.html

  //Arduino ??? pinMode????2???INPUT_PULLUP http://mag.switch-science.com/2013/05/23/input_pullup/

  pinMode(inPin, INPUT_PULLUP);// ????????????

  lastTime = millis();

}



void loop()

{

  //TODO attachInterrupt(interrupt, function, mode) http://www.musashinodenpa.com/arduino/ref/index.php?f=0&pos=3045

  //Arduino Hall Effect Sensor Project http://diyhacking.com/projects/ArduinoHallEffect.ino

  hallVal = digitalRead(inPin);  // ???????

  if ( hallVal != lasthallVal) {

    lasthallVal = hallVal;

    if (hallVal == 1) {

      hallCount++;

    }

  }



  //Bt????

  if (servoAttached && lastTime > millis() + 1100) {

    sv9.writeMicroseconds(1500);

    sv10.writeMicroseconds(1500);

  }



  int ret;

  if ( Serial.available() > 0 ) {

    lastTime = millis();

    digitalWrite(13, HIGH); //LED??

    int d = Serial.read();



    if ( d == 'a' ) {

      sv9.attach(9, 800, 2200);

      sv10.attach(10, 800, 2200);

      sv5.attach(5, 800, 2200);

      sv6.attach(6, 800, 2200);

      servoAttached = true;

      Serial.println("Servo Attached");

      hallCount = 0;

    }

    else if ( d == 'd' ) {

      sv9.detach();

      sv10.detach();

      sv5.detach();

      sv6.detach();

      servoAttached = false;

      Serial.println("Servo Detached");

    }

    else if ( d == 'r' ) {

      if (hallCount != 0) {

        Serial.println("RPS:" + String(hallCount, DEC));

        //"Servo: " + String(sv9.read(), DEC) + " : " + String(sv10.read(), DEC));

        hallCount = 0;

      } else { //A0 Batt Volte

        int batValue = analogRead(A0);

        Serial.println("BAT:" + String(batValue, DEC));

      }

    }

    else if ( '0' <= d && d <= '9' ) {

      d -= '0';

      if (i == 7) {

        analog9 = d * 1000;

      }

      if (i == 6) {

        analog9 += d * 100;

      }

      if (i == 5) {

        analog9 += d * 10;

      }

      if (i == 4) {

        analog9 += d;

      }

      if (i == 3) {

        analog10 = d * 1000;

      }

      if (i == 2) {

        analog10 += d * 100;

      }

      if (i == 1) {

        analog10 += d * 10;

      }

      if (i == 0) {

        analog10 += d;

        //Serial.println("analog9  : " + String(analog9, DEC));

        //Serial.println("analog10 : " + String(analog10, DEC));

      }

      i--;

    }

    else if ( d == 'm' ) {

      sv9.writeMicroseconds(analog9);

      sv10.writeMicroseconds(analog10);

      //Serial.println("sv 9 Move to ms: " + String(analog9, DEC));

      //Serial.println("sv10 Move to ms: " + String(analog10, DEC));

      analog9 = 0;

      analog10 = 0;

      i = 7;

    } else if ( d == 'x' ) {

      //sv5.writeMicroseconds(analog9);

      moveShaft(sv5, analog9, 5);

      //Serial.println("camera x  : " + String(analog9, DEC));

      analog9 = 0;

      i = 7;

    } else if ( d == 'y' ) {

      //sv6.writeMicroseconds(analog9);

      moveShaft(sv6, analog9, 5);

      //Serial.println("camera y  : " + String(analog9, DEC));

      analog9 = 0;

      i = 7;

    }

    digitalWrite(13, LOW);   //LED??

  }

}
